// Digital circuit bloco4bits.dig as structural Verilog
module bloco4bits (
  input  I0,
  input  I1,
  input  I2,
  input  I3,
  input  L,
  output O0,
  output O1,
  output O2,
  output O3
);

  assign O0 = L ? I0 : 1'bz;  // Driver driver_1
  assign O1 = L ? I1 : 1'bz;  // Driver driver_2
  assign O2 = L ? I2 : 1'bz;  // Driver driver_3
  assign O3 = L ? I3 : 1'bz;  // Driver driver_4
endmodule
